# Fritzing sketch extended-fritzing-layout (saved by Fritzing 0.8.3b)
breadboards: 2

parts:
  Bauteil1 = Arduino Uno (Rev3)
  D1 = LED_BARGRAPH_10 [package=led_bargaph_10]
  Decade_Counter_4017 = IC, DIP package, 16 pins [chip_label=IC]

nets:
  N1: Bauteil1.GND, D1.J_C, D1.I_C, D1.H_C, D1.G_C, D1.F_C, D1.E_C, D1.D_C, D1.C_C, D1.B_C, D1.A_C, Decade_Counter_4017.pin8
  N2: Bauteil1.D8, Decade_Counter_4017.pin15
  N3: Bauteil1.D9_PWM, Decade_Counter_4017.pin13
  N4: Bauteil1.D10_PWM/SS, Decade_Counter_4017.pin12
  N5: Bauteil1.D2, Decade_Counter_4017.pin14
  N6: Bauteil1.5V, Decade_Counter_4017.pin16
  N7: D1.A_A, Decade_Counter_4017.pin3
  N8: D1.B_A, Decade_Counter_4017.pin2
  N9: D1.C_A, Decade_Counter_4017.pin4
  N10: D1.D_A, Decade_Counter_4017.pin7
  N11: D1.E_A, Decade_Counter_4017.pin10
  N12: D1.F_A, Decade_Counter_4017.pin1
  N13: D1.G_A, Decade_Counter_4017.pin5
  N14: D1.H_A, Decade_Counter_4017.pin6
  N15: D1.I_A, Decade_Counter_4017.pin9
  N16: D1.J_A, Decade_Counter_4017.pin11
